# Fritzing sketch binary_counter (saved by Fritzing 0.9.0b)
breadboards: 1

parts:
  Part1 = Arduino Uno (Rev3) - ICSP
  LED1 = LED - 5mm [color="Red (633nm)" package="5 mm [THT]"]
  LED2 = LED - 5mm [color="Red (633nm)" package="5 mm [THT]"]
  LED3 = LED - 5mm [color="Red (633nm)" package="5 mm [THT]"]
  LED4 = LED - 5mm [color="Red (633nm)" package="5 mm [THT]"]
  R1 = Resistor [tolerance=±5% resistance=220 package=THT]
  R2 = Resistor [tolerance=±5% resistance=220 package=THT]
  R3 = Resistor [tolerance=±5% resistance=220 package=THT]
  R4 = Resistor [tolerance=±5% resistance=220 package=THT]

nets:
  N1: Part1.ICSP_MOSI, Part1.D11_PWM/MOSI, LED4.cathode
  N2: Part1.D8, LED1.cathode
  N3: Part1.D9_PWM, LED2.cathode
  N4: Part1.D10_PWM/SS, LED3.cathode
  N5: Part1.GND, R1.Pin_1, R2.Pin_1, R3.Pin_1, R4.Pin_1
  N6: LED1.anode, R1.Pin_0
  N7: LED2.anode, R2.Pin_0
  N8: LED3.anode, R3.Pin_0
  N9: LED4.anode, R4.Pin_0
